# Fritzing sketch WaterLevelGuard_Schematic (saved by Fritzing 0.9.3b)
breadboards: 1

parts:
  Part1 = Arduino Nano (Rev3.0)
  LED1 = RGB LED (com. cathode, rgb) [package="5 mm [THT]"]
  Part2 = Soil Moisture Sensor

nets:
  GND: Part1.GND, LED1.blue_anode, Part2.GND
  N1: Part1.D2, LED1.green_anode
  N2: Part1.D3, LED1.common_cathode
  N3: Part1.D4, LED1.red_anode
